// Logisim project rs_latch.circ as structural Verilog: 1 circuit, main circuit main
module main (
  input  R,
  input  S,
  output Q,
  output Qn
);

  nor nor_1 (Q, R, Qn);
  nor nor_2 (Qn, Q, S);

  // Notes on the sheet:
  //   Problem 1 - RS Latch (NOR)
endmodule
