// Logisim project d_latch.circ as structural Verilog: 1 circuit, main circuit main
module main (
  input  D,
  input  en,
  output Q,
  output Qn
);

  wire nand_1_out, nand_2_out;

  nand nand_1 (nand_1_out, D, en);
  nand nand_2 (nand_2_out, nand_1_out, en);
  nand nand_3 (Q, nand_1_out, Qn);
  nand nand_4 (Qn, Q, nand_2_out);

  // Notes on the sheet:
  //   Problem 2 - D Latch (NAND)
endmodule
