// Logisim project d_ff.circ as structural Verilog: 1 circuit, main circuit main
module main (
  input  D,
  input  clk,
  output Q,
  output Qn
);

  wire nand_1_out, nand_2_out, nand_3_out, nand_4_out, nand_5_out, nand_6_out, not_1_out;

  not not_1 (not_1_out, clk);
  nand nand_1 (nand_1_out, D, not_1_out);
  nand nand_2 (nand_2_out, nand_1_out, not_1_out);
  nand nand_3 (nand_3_out, nand_1_out, nand_4_out);
  nand nand_4 (nand_4_out, nand_3_out, nand_2_out);
  nand nand_5 (nand_5_out, nand_3_out, clk);
  nand nand_6 (nand_6_out, nand_5_out, clk);
  nand nand_7 (Q, nand_5_out, Qn);
  nand nand_8 (Qn, Q, nand_6_out);

  // Notes on the sheet:
  //   Problem 3 - Master-Slave D Flip-Flop (2 x NAND D Latch + Inverter)
endmodule
