// Logisim project jk_ff.circ as structural Verilog: 1 circuit, main circuit main
module main (
  input  clk,
  input  J,
  input  K,
  input  clr,
  output Q,
  output Qn
);

  wire nand_1_out, nand_2_out, nand_3_out, nand_4_out, nand_5_out, nand_6_out, nand_7_out, not_1_out,
       not_2_out;

  not not_1 (not_1_out, K);
  not not_2 (not_2_out, clr);
  nand nand_1 (nand_1_out, J, Qn);
  nand nand_2 (nand_2_out, not_1_out, Q);
  nand nand_3 (nand_3_out, nand_1_out, nand_2_out);
  nand nand_4 (nand_4_out, nand_7_out, nand_5_out);
  nand nand_5 (nand_5_out, nand_4_out, clk, not_2_out);
  nand nand_6 (nand_6_out, nand_5_out, clk, nand_7_out);
  nand nand_7 (nand_7_out, nand_6_out, nand_3_out, not_2_out);
  nand nand_8 (Q, nand_5_out, Qn);
  nand nand_9 (Qn, Q, nand_6_out, not_2_out);

  // Notes on the sheet:
  //   Problem 4 - JK Flip-Flop (NAND edge-triggered, D = J*Qn + Kn*Q, async clr)
endmodule
