// Logisim project d_ff_sc.circ as structural Verilog: 1 circuit, main circuit main
module main (
  input  set,
  input  clk,
  input  D,
  input  clr,
  output Q,
  output Qn
);

  wire nand_1_out, nand_2_out, nand_3_out, nand_4_out, nand_5_out, not_1_out;

  not not_1 (not_1_out, clr);
  nand nand_1 (nand_1_out, set, not_1_out);
  nand nand_2 (nand_2_out, nand_1_out, nand_5_out, nand_3_out);
  nand nand_3 (nand_3_out, nand_2_out, clk, not_1_out);
  nand nand_4 (nand_4_out, nand_3_out, clk, nand_5_out);
  nand nand_5 (nand_5_out, nand_4_out, D, not_1_out);
  nand nand_6 (Q, nand_1_out, nand_3_out, Qn);
  nand nand_7 (Qn, Q, nand_4_out, not_1_out);

  // Notes on the sheet:
  //   Problem 5 - D Flip-Flop with Async Set / Clear (Clear priority)
endmodule
